// Logisim project RUSaT.circ as structural Verilog
module main (
  output [15:0] out_1
);

  wire alu_1_zerobit, and_1_out, and_2_out, clock_1_out, controlunit_1_alu_src, controlunit_1_cbnz,
       controlunit_1_cbz, controlunit_1_halt, controlunit_1_mem_read, controlunit_1_mem_write,
       controlunit_1_reg_write, controlunit_1_reg_write2, controlunit_1_sign_extend, controlunit_1_ubr,
       controlunit_1_use_pc, not_1_out, or_1_out;
  wire [0:0] or_2_out;
  wire [1:0] controlunit_1_mem_size;
  wire [2:0] instructionfetch_1_rd, instructionfetch_1_rm, instructionfetch_1_rn;
  wire [6:0] instructionfetch_1_opcode;
  wire [7:0] extracteightbits_1_output16;
  wire [15:0] adder_1_out, adder_2_out, extractsixteenbits_1_outputbits, instructionfetch_1_imm,
       multiplexer_1_out, pc_1_pc_instr_mem;
  wire [63:0] alu_1_aluout, alu_2_aluout, alusrca_1_out_6, alusrcb_1_out_6, datamem_1_finaloutput,
       projectregisters_1_regdata1, projectregisters_1_regdata2, projectregisters_1_regdata3,
       writeback_1_wboutput, writeback_2_wboutput;

  Adder #(.width(16)) adder_1 (.a(16'h4), .b(out_1), .out(adder_1_out));  // open: cin, cout
  Adder #(.width(16)) adder_2 (.a(out_1), .b(instructionfetch_1_imm), .out(adder_2_out));  // open: cin, cout
  Multiplexer #(.select(2), .width(16)) multiplexer_1 (
    .in0(adder_1_out), .in1(adder_2_out), .out(multiplexer_1_out), .sel({1'b0, or_2_out[0]}));  // open: in2, in3
  and and_1 (and_1_out, controlunit_1_cbnz, ~alu_1_zerobit);  // AND_Gate
  and and_2 (and_2_out, controlunit_1_cbz, alu_1_zerobit);
  or or_1 (or_1_out, and_1_out, and_2_out);
  Clock clock_1 (.out(clock_1_out));
  or or_2 (or_2_out[0], or_1_out, controlunit_1_ubr);
  ControlUnit controlunit_1 (
    .OPCODE(instructionfetch_1_opcode), .ALU_SRC(controlunit_1_alu_src), .REG_WRITE(controlunit_1_reg_write),
    .REG_WRITE2(controlunit_1_reg_write2), .MEM_READ(controlunit_1_mem_read),
    .MEM_WRITE(controlunit_1_mem_write), .SIGN_EXTEND(controlunit_1_sign_extend),
    .MEM_SIZE(controlunit_1_mem_size), .USE_PC(controlunit_1_use_pc), .UBr(controlunit_1_ubr),
    .CBZ(controlunit_1_cbz), .CBNZ(controlunit_1_cbnz), .HALT(controlunit_1_halt));
  ExtractEightBits extracteightbits_1 (.InputA(projectregisters_1_regdata3), .Output16(extracteightbits_1_output16));
  ExtractSixteenBits extractsixteenbits_1 (.InputA(alu_1_aluout), .OutputBits(extractsixteenbits_1_outputbits));
  not not_1 (not_1_out, controlunit_1_mem_read);
  ALUsrcA alusrca_1 (
    .PC(out_1), .RegData1(projectregisters_1_regdata1), .RegData3(projectregisters_1_regdata3),
    .USE_RegData3(controlunit_1_reg_write2), .USE_PC(controlunit_1_use_pc), .out_6(alusrca_1_out_6));
  ALU alu_1 (
    .InputB(alusrcb_1_out_6), .InputA(alusrca_1_out_6), .ALUnum(1'b0), .OPCODE(instructionfetch_1_opcode),
    .ALUout(alu_1_aluout), .ZeroBit(alu_1_zerobit));
  PC pc_1 (
    .PC_new(multiplexer_1_out), .HALT(controlunit_1_halt), .CLK(clock_1_out), .PC_ACTUAL(out_1),
    .PC_INSTR_MEM(pc_1_pc_instr_mem));
  DataMem datamem_1 (
    .ClockTick(clock_1_out), .MemSize(controlunit_1_mem_size), .MemAdr(extractsixteenbits_1_outputbits),
    .SignedExtension(controlunit_1_sign_extend), .MemW(controlunit_1_mem_write),
    .MemR(controlunit_1_mem_read), .DataW(extracteightbits_1_output16), .FinalOutput(datamem_1_finaloutput));
  InstructionFetch instructionfetch_1 (
    .PC_INSTRUCTION_MEM(pc_1_pc_instr_mem), .Rd(instructionfetch_1_rd), .Rn(instructionfetch_1_rn),
    .Rm(instructionfetch_1_rm), .IMM(instructionfetch_1_imm), .OPCODE(instructionfetch_1_opcode));
  ALUsrcB alusrcb_1 (
    .IMM(instructionfetch_1_imm), .RegData1(projectregisters_1_regdata1),
    .RegData2(projectregisters_1_regdata2), .USE_RegData1(controlunit_1_reg_write2),
    .ALU_SRCB(controlunit_1_alu_src), .out_6(alusrcb_1_out_6));
  ALU alu_2 (
    .InputB(alusrcb_1_out_6), .InputA(alusrca_1_out_6), .ALUnum(1'b1), .OPCODE(instructionfetch_1_opcode),
    .ALUout(alu_2_aluout));  // open: ZeroBit
  ProjectRegisters projectregisters_1 (
    .ClockTick(clock_1_out), .ReadReg1(instructionfetch_1_rn), .ReadReg2(instructionfetch_1_rm),
    .ReadReg3(instructionfetch_1_rd), .WriteReg1(instructionfetch_1_rd), .RegWrite1(controlunit_1_reg_write),
    .WriteReg2(instructionfetch_1_rn), .RegWrite2(controlunit_1_reg_write2),
    .RegDataW1(writeback_1_wboutput), .RegDataW2(writeback_2_wboutput),
    .RegData1(projectregisters_1_regdata1), .RegData2(projectregisters_1_regdata2),
    .RegData3(projectregisters_1_regdata3));
  WriteBack writeback_1 (
    .MemOutput(datamem_1_finaloutput), .ALUoutput(alu_1_aluout), .WriteALU(not_1_out),
    .WBOutput(writeback_1_wboutput));
  WriteBack writeback_2 (
    .MemOutput(datamem_1_finaloutput), .ALUoutput(alu_2_aluout), .WriteALU(not_1_out),
    .WBOutput(writeback_2_wboutput));

  // Notes on the sheet:
  //   Dan Liu & Amartya Kalra
  //   I pledge my honor that I have abided by the Stevens Honor System.
  //   RUSaT
endmodule

module InstructionMem (
  input  [15:0] ProgramCounterAdr,
  output [31:0] ActualInstruction
);

  // ROM #(.addrWidth(16), .line("quad")) rom_1: pin names not known; wires that end beside it: ProgramCounterAdr, ActualInstruction[7:0], ActualInstruction[15:8], ActualInstruction[23:16], ActualInstruction[31:24]

  // Notes on the sheet:
  //   ProgramCounterAdr: initial=0x80
  //   contents of rom_1 (hex, n*v repeats v):
  //   2 0 ff d5 0 8 ff d5 10 0 0 da 3 8 ff d5 c1 0 0 8 8 28 0 e8 9 2 0 8c d1 0 0 40 1b 2 0 84 8 d8 ff f1
endmodule

module DataMem (
  input  ClockTick,
  input  [1:0] MemSize,
  input  [15:0] MemAdr,
  input  SignedExtension,
  input  MemW,
  input  MemR,
  input  [7:0] DataW,
  output [63:0] FinalOutput
);

  wire [7:0] RAM_CHIP_dout;
  wire [63:0] normalbitextender_1_normaloutput, signedbitextender_1_signedoutput;

  RAM #(.addrWidth(16), .asyncread("true"), .trigger("falling")) RAM_CHIP (
    .addr(MemAdr), .we(MemW), .oe(MemR), .clk(ClockTick), .din(DataW), .dout(RAM_CHIP_dout));
  NormalBitExtender normalbitextender_1 (
    .EightBitInput(RAM_CHIP_dout), .NormalOutput(normalbitextender_1_normaloutput));
  SignedBitExtender signedbitextender_1 (
    .EightBitInput(RAM_CHIP_dout), .SignedOutput(signedbitextender_1_signedoutput));
  Multiplexer #(.width(64)) multiplexer_1 (
    .in0(normalbitextender_1_normaloutput), .in1(signedbitextender_1_signedoutput), .out(FinalOutput),
    .sel(SignedExtension));

  // Notes on the sheet:
  //   Keep Mem Size as input if our Ram Chip changes to be used for 64 bit properly.
endmodule

module PC (
  input  [15:0] PC_new,
  input  HALT,
  input  CLK,
  output [15:0] PC_ACTUAL,
  output [15:0] PC_INSTR_MEM
);

  wire not_1_out, s_r_ff_1_q, s_r_ff_2_q;
  wire [15:0] register_1_q;

  not not_1 (not_1_out, HALT);
  Register #(.width(16)) register_1 (.D(PC_new), .en(not_1_out), .clk(CLK), .Q(register_1_q));  // open: clr
  S_R_Flip_Flop s_r_ff_1 (.S(1'b1), .R(1'b0), .clk(CLK), .Q(s_r_ff_1_q));  // open: reset, Qn, preset
  S_R_Flip_Flop s_r_ff_2 (.S(s_r_ff_1_q), .R(1'b0), .clk(CLK), .Q(s_r_ff_2_q));  // open: reset, Qn, preset
  Multiplexer #(.width(16)) multiplexer_1 (.in0(16'h80), .in1(register_1_q), .out(PC_ACTUAL), .sel(s_r_ff_2_q));
  Subtractor #(.width(16)) subtractor_1 (.a(PC_ACTUAL), .b(16'h80), .out(PC_INSTR_MEM));  // open: bin, bout
endmodule

module InstructionFetch (
  input  [15:0] PC_INSTRUCTION_MEM,
  output [2:0] Rd,
  output [2:0] Rn,
  output [2:0] Rm,
  output [15:0] IMM,
  output [6:0] OPCODE
);

  InstructionMem instructionmem_1 (
    .ProgramCounterAdr(PC_INSTRUCTION_MEM), .ActualInstruction({OPCODE, IMM, Rm, Rn, Rd}));

  // Notes on the sheet:
  //   PC_INSTRUCTION_MEM: initial=0x80
endmodule

module ProjectRegisters (
  input  ClockTick,
  input  [2:0] ReadReg1,
  input  [2:0] ReadReg2,
  input  [2:0] ReadReg3,
  input  [2:0] WriteReg1,
  input  RegWrite1,
  input  [2:0] WriteReg2,
  input  RegWrite2,
  input  [63:0] RegDataW1,
  input  [63:0] RegDataW2,
  output [63:0] RegData1,
  output [63:0] RegData2,
  output [63:0] RegData3
);

  wire and_1_out, and_2_out, and_3_out, and_4_out, and_5_out, and_6_out, and_7_out, and_8_out, and_9_out,
       and_10_out, and_11_out, and_12_out, and_13_out, and_14_out, and_15_out, and_16_out, decoder_1_out0,
       decoder_1_out1, decoder_1_out2, decoder_1_out3, decoder_1_out4, decoder_1_out5, decoder_1_out6,
       decoder_1_out7, decoder_2_out0, decoder_2_out1, decoder_2_out2, decoder_2_out3, decoder_2_out4,
       decoder_2_out5, decoder_2_out6, decoder_2_out7, or_1_out, or_2_out, or_3_out, or_4_out, or_5_out,
       or_6_out, or_7_out;
  wire [63:0] multiplexer_1_out, multiplexer_2_out, multiplexer_3_out, multiplexer_4_out, multiplexer_5_out,
       multiplexer_6_out, multiplexer_7_out, multiplexer_8_out, register_1_q, register_2_q, register_3_q,
       register_4_q, register_5_q, register_6_q, register_7_q, register_8_q;

  Decoder #(.enable("false"), .select(3)) decoder_1 (
    .out0(decoder_1_out0), .out1(decoder_1_out1), .out2(decoder_1_out2), .out3(decoder_1_out3),
    .out4(decoder_1_out4), .out5(decoder_1_out5), .out6(decoder_1_out6), .out7(decoder_1_out7),
    .sel(WriteReg1));
  Decoder #(.enable("false"), .select(3)) decoder_2 (
    .out0(decoder_2_out0), .out1(decoder_2_out1), .out2(decoder_2_out2), .out3(decoder_2_out3),
    .out4(decoder_2_out4), .out5(decoder_2_out5), .out6(decoder_2_out6), .out7(decoder_2_out7),
    .sel(WriteReg2));
  and and_1 (and_1_out, decoder_1_out0, RegWrite1);
  and and_2 (and_2_out, decoder_1_out1, RegWrite1);
  and and_3 (and_3_out, decoder_1_out2, RegWrite1);
  and and_4 (and_4_out, decoder_1_out3, RegWrite1);
  and and_5 (and_5_out, decoder_1_out4, RegWrite1);
  and and_6 (and_6_out, decoder_1_out5, RegWrite1);
  and and_7 (and_7_out, decoder_1_out6, RegWrite1);
  and and_8 (and_8_out, decoder_1_out7, RegWrite1);
  and and_9 (and_9_out, decoder_2_out0, RegWrite2);
  and and_10 (and_10_out, decoder_2_out1, RegWrite2);
  and and_11 (and_11_out, decoder_2_out2, RegWrite2);
  and and_12 (and_12_out, decoder_2_out3, RegWrite2);
  and and_13 (and_13_out, decoder_2_out4, RegWrite2);
  and and_14 (and_14_out, decoder_2_out5, RegWrite2);
  and and_15 (and_15_out, decoder_2_out6, RegWrite2);
  and and_16 (and_16_out, decoder_2_out7, RegWrite2);
  or or_1 (or_1_out, and_1_out, and_9_out);
  or or_2 (or_2_out, and_2_out, and_10_out);
  or or_3 (or_3_out, and_3_out, and_11_out);
  or or_4 (or_4_out, and_4_out, and_12_out);
  or or_5 (or_5_out, and_5_out, and_13_out);
  or or_6 (or_6_out, and_6_out, and_14_out);
  or or_7 (or_7_out, and_7_out, and_15_out);
  // OR_Gate or_8 has open pins: in0=and_8_out, in1=and_16_out, out=open
  Multiplexer #(.width(64)) multiplexer_1 (.in0(RegDataW1), .in1(RegDataW2), .out(multiplexer_1_out), .sel(and_9_out));
  Multiplexer #(.width(64)) multiplexer_2 (.in0(RegDataW1), .in1(RegDataW2), .out(multiplexer_2_out), .sel(and_10_out));
  Multiplexer #(.width(64)) multiplexer_3 (.in0(RegDataW1), .in1(RegDataW2), .out(multiplexer_3_out), .sel(and_11_out));
  Multiplexer #(.width(64)) multiplexer_4 (.in0(RegDataW1), .in1(RegDataW2), .out(multiplexer_4_out), .sel(and_12_out));
  Multiplexer #(.width(64)) multiplexer_5 (.in0(RegDataW1), .in1(RegDataW2), .out(multiplexer_5_out), .sel(and_13_out));
  Multiplexer #(.width(64)) multiplexer_6 (.in0(RegDataW1), .in1(RegDataW2), .out(multiplexer_6_out), .sel(and_14_out));
  Multiplexer #(.width(64)) multiplexer_7 (.in0(RegDataW1), .in1(RegDataW2), .out(multiplexer_7_out), .sel(and_15_out));
  Multiplexer #(.width(64)) multiplexer_8 (.in0(RegDataW1), .in1(RegDataW2), .out(multiplexer_8_out));  // open: sel
  Register #(.width(64)) register_1 (
    .D(multiplexer_1_out), .en(or_1_out), .clk(ClockTick), .Q(register_1_q));  // open: clr
  Register #(.width(64)) register_2 (
    .D(multiplexer_2_out), .en(or_2_out), .clk(ClockTick), .Q(register_2_q));  // open: clr
  Register #(.width(64)) register_3 (
    .D(multiplexer_3_out), .en(or_3_out), .clk(ClockTick), .Q(register_3_q));  // open: clr
  Register #(.width(64)) register_4 (
    .D(multiplexer_4_out), .en(or_4_out), .clk(ClockTick), .Q(register_4_q));  // open: clr
  Register #(.width(64)) register_5 (
    .D(multiplexer_5_out), .en(or_5_out), .clk(ClockTick), .Q(register_5_q));  // open: clr
  Register #(.width(64)) register_6 (
    .D(multiplexer_6_out), .en(or_6_out), .clk(ClockTick), .Q(register_6_q));  // open: clr
  Register #(.width(64)) register_7 (
    .D(multiplexer_7_out), .en(or_7_out), .clk(ClockTick), .Q(register_7_q));  // open: clr
  Register #(.width(64)) register_8 (.D(multiplexer_8_out), .en(1'b0), .clk(ClockTick), .Q(register_8_q));  // open: clr
  Multiplexer #(.select(3), .width(64)) multiplexer_9 (
    .in0(register_1_q), .in1(register_2_q), .in2(register_3_q), .in3(register_4_q), .in4(register_5_q),
    .in5(register_6_q), .in6(register_7_q), .in7(register_8_q), .out(RegData1), .sel(ReadReg1));
  Multiplexer #(.select(3), .width(64)) multiplexer_10 (
    .in0(register_1_q), .in1(register_2_q), .in2(register_3_q), .in3(register_4_q), .in4(register_5_q),
    .in5(register_6_q), .in6(register_7_q), .in7(register_8_q), .out(RegData2), .sel(ReadReg2));
  Multiplexer #(.select(3), .width(64)) multiplexer_11 (
    .in0(register_1_q), .in1(register_2_q), .in2(register_3_q), .in3(register_4_q), .in4(register_5_q),
    .in5(register_6_q), .in6(register_7_q), .in7(register_8_q), .out(RegData3), .sel(ReadReg3));
endmodule

module ControlUnit (
  input  [6:0] OPCODE,
  output ALU_SRC,
  output REG_WRITE,
  output REG_WRITE2,
  output MEM_READ,
  output MEM_WRITE,
  output SIGN_EXTEND,
  output [1:0] MEM_SIZE,
  output USE_PC,
  output UBr,
  output CBZ,
  output CBNZ,
  output HALT
);

  wire and_1_out, and_2_out, and_5_out, nor_1_out, nor_2_out;
  wire [1:0] adder_1_out;

  and and_1 (and_1_out, ~OPCODE[6], OPCODE[5], ~OPCODE[4]);  // AND_Gate
  and and_2 (and_2_out, OPCODE[6], OPCODE[5], OPCODE[4]);
  and and_3 (MEM_WRITE, ~OPCODE[6], OPCODE[5]);  // AND_Gate
  nor nor_1 (nor_1_out, OPCODE[6], OPCODE[5], OPCODE[4], OPCODE[3], OPCODE[2]);
  nor nor_2 (nor_2_out, OPCODE[6], OPCODE[5]);
  and and_4 (SIGN_EXTEND, ~OPCODE[6], ~OPCODE[5], OPCODE[4]);  // AND_Gate
  and and_5 (and_5_out, ~OPCODE[6], OPCODE[5], ~OPCODE[4]);  // AND_Gate
  nor nor_3 (REG_WRITE, nor_1_out, and_1_out, and_2_out);
  Adder #(.width(2)) adder_1 (.a(OPCODE[3:2]), .b(2'b11), .out(adder_1_out));  // open: cin, cout
  Multiplexer #(.width(2)) multiplexer_1 (.in0(adder_1_out), .in1(OPCODE[3:2]), .out(MEM_SIZE), .sel(and_5_out));
  SevenBitZeroCheck sevenbitzerocheck_1 (.Bits(OPCODE), .Is_Zero(HALT));
  or or_1 (MEM_READ, USE_PC, nor_2_out);
  and and_6 (USE_PC, OPCODE[6], OPCODE[5], ~OPCODE[4], OPCODE[3], ~OPCODE[2], OPCODE[1], ~OPCODE[0]);  // AND_Gate
  and and_7 (UBr, OPCODE[6], OPCODE[5], OPCODE[4], ~OPCODE[3], ~OPCODE[2], ~OPCODE[1], ~OPCODE[0]);  // AND_Gate
  and and_8 (CBZ, OPCODE[6], OPCODE[5], OPCODE[4], ~OPCODE[3], OPCODE[2], ~OPCODE[1], ~OPCODE[0]);  // AND_Gate
  and and_9 (CBNZ, OPCODE[6], OPCODE[5], OPCODE[4], OPCODE[3], ~OPCODE[2], ~OPCODE[1], ~OPCODE[0]);  // AND_Gate

  assign ALU_SRC = OPCODE[1];
  assign REG_WRITE2 = OPCODE[0];

  // Notes on the sheet:
  //   use 2nd write port (swap only)
  //   alusrc (imm:1, reg:0)
  //   00 = 1 byte, 01 = 2 bytes, 10 = 4 bytes, 11 = 8 bytes
endmodule

module ALUsrcA (
  input  [15:0] PC,
  input  [63:0] RegData1,
  input  [63:0] RegData3,
  input  USE_RegData3,
  input  USE_PC,
  output [63:0] out_6
);

  Multiplexer #(.select(2), .width(64)) multiplexer_1 (
    .in0(RegData1), .in1(RegData3), .in2({{48{1'b0}}, PC}), .in3({{48{1'b0}}, PC}), .out(out_6),
    .sel({USE_PC, USE_RegData3}));
endmodule

module ALUsrcB (
  input  [15:0] IMM,
  input  [63:0] RegData1,
  input  [63:0] RegData2,
  input  USE_RegData1,
  input  ALU_SRCB,
  output [63:0] out_6
);

  wire [63:0] signedbitextender2_1_outputa;

  SignedBitExtender2 signedbitextender2_1 (.InputA(IMM), .OutputA(signedbitextender2_1_outputa));
  Multiplexer #(.select(2), .width(64)) multiplexer_1 (
    .in0(RegData2), .in1(signedbitextender2_1_outputa), .in2(RegData1), .in3(RegData1), .out(out_6),
    .sel({USE_RegData1, ALU_SRCB}));
endmodule

module ALUctrl (
  input  SWAP_bit,
  input  [3:0] Bundled_Bits,
  input  ALUsrc,
  input  Nonmem_vs_Mem,
  output SwapSignal,
  output HaltSignal,
  output AddSignal,
  output LD1Signal,
  output SubtractSignal,
  output LD2Signal,
  output MultiplySignal,
  output LD4Signal,
  output DivisionSignal,
  output LDSignal,
  output ModulusSignal,
  output LD1SSignal,
  output ASRSignal,
  output LD2SSignal,
  output LSLSignal,
  output LD4SSignal,
  output ANDSignal,
  output ST1Signal,
  output ORSignal,
  output ST2Signal,
  output NegSignal,
  output ST4Signal,
  output LD_IMMSignal,
  output STSignal,
  output BSignal,
  output CBZSignal,
  output CBNZSignal
);

  wire fourbitcompar_1_equal, fourbitcompar_2_equal, fourbitcompar_3_equal, fourbitcompar_4_equal,
       fourbitcompar_5_equal, fourbitcompar_6_equal, fourbitcompar_7_equal, fourbitcompar_8_equal,
       fourbitcompar_9_equal, fourbitcompar_10_equal, fourbitcompar_11_equal, fourbitcompar_12_equal,
       fourbitcompar_13_equal, fourbitcompar_14_equal, fourbitcompar_15_equal;

  SevenBitZeroCheck sevenbitzerocheck_1 (.Bits({Nonmem_vs_Mem, ALUsrc, Bundled_Bits, SWAP_bit}), .Is_Zero(HaltSignal));
  FourBitCompar fourbitcompar_1 (.Value(4'b0000), .Bits(Bundled_Bits), .Equal(fourbitcompar_1_equal));
  FourBitCompar fourbitcompar_2 (.Value(4'b0001), .Bits(Bundled_Bits), .Equal(fourbitcompar_2_equal));
  FourBitCompar fourbitcompar_3 (.Value(4'b0010), .Bits(Bundled_Bits), .Equal(fourbitcompar_3_equal));
  FourBitCompar fourbitcompar_4 (.Value(4'b0011), .Bits(Bundled_Bits), .Equal(fourbitcompar_4_equal));
  FourBitCompar fourbitcompar_5 (.Value(4'b0100), .Bits(Bundled_Bits), .Equal(fourbitcompar_5_equal));
  FourBitCompar fourbitcompar_6 (.Value(4'b0101), .Bits(Bundled_Bits), .Equal(fourbitcompar_6_equal));
  FourBitCompar fourbitcompar_7 (.Value(4'b0110), .Bits(Bundled_Bits), .Equal(fourbitcompar_7_equal));
  FourBitCompar fourbitcompar_8 (.Value(4'b0111), .Bits(Bundled_Bits), .Equal(fourbitcompar_8_equal));
  FourBitCompar fourbitcompar_9 (.Value(4'b1000), .Bits(Bundled_Bits), .Equal(fourbitcompar_9_equal));
  FourBitCompar fourbitcompar_10 (.Value(4'b1001), .Bits(Bundled_Bits), .Equal(fourbitcompar_10_equal));
  FourBitCompar fourbitcompar_11 (.Value(4'b1010), .Bits(Bundled_Bits), .Equal(fourbitcompar_11_equal));
  FourBitCompar fourbitcompar_12 (.Value(4'b1011), .Bits(Bundled_Bits), .Equal(fourbitcompar_12_equal));
  FourBitCompar fourbitcompar_13 (.Value(4'b1100), .Bits(Bundled_Bits), .Equal(fourbitcompar_13_equal));
  FourBitCompar fourbitcompar_14 (.Value(4'b1101), .Bits(Bundled_Bits), .Equal(fourbitcompar_14_equal));
  FourBitCompar fourbitcompar_15 (.Value(4'b1110), .Bits(Bundled_Bits), .Equal(fourbitcompar_15_equal));
  // XOR_Gate xor_1 has open pins: in0=fourbitcompar_1_equal, in1=ALUsrc, out=open
  and and_1 (AddSignal, fourbitcompar_1_equal, ALUsrc);
  xor xor_2 (LD1Signal, fourbitcompar_2_equal, ALUsrc);
  and and_2 (SubtractSignal, fourbitcompar_2_equal, ALUsrc);
  xor xor_3 (LD2Signal, fourbitcompar_3_equal, ALUsrc);
  and and_3 (MultiplySignal, fourbitcompar_3_equal, ALUsrc);
  xor xor_4 (LD4Signal, fourbitcompar_4_equal, ALUsrc);
  xor xor_5 (LDSignal, fourbitcompar_5_equal, ALUsrc);
  xor xor_6 (LD1SSignal, fourbitcompar_6_equal, ALUsrc);
  xor xor_7 (LD2SSignal, fourbitcompar_7_equal, ALUsrc);
  xor xor_8 (LD4SSignal, fourbitcompar_8_equal, ALUsrc);
  xor xor_9 (ST1Signal, fourbitcompar_9_equal, ALUsrc);
  xor xor_10 (ST2Signal, fourbitcompar_10_equal, ALUsrc);
  xor xor_11 (ST4Signal, fourbitcompar_11_equal, ALUsrc);
  xor xor_12 (STSignal, fourbitcompar_12_equal, ALUsrc);
  and and_4 (DivisionSignal, fourbitcompar_4_equal, ALUsrc);
  and and_5 (ModulusSignal, fourbitcompar_5_equal, ALUsrc);
  and and_6 (ASRSignal, fourbitcompar_6_equal, ALUsrc);
  and and_7 (LSLSignal, fourbitcompar_7_equal, ALUsrc);
  and and_8 (ANDSignal, fourbitcompar_8_equal, ALUsrc);
  and and_9 (ORSignal, fourbitcompar_9_equal, ALUsrc);
  and and_10 (NegSignal, fourbitcompar_10_equal, ALUsrc);
  and and_11 (LD_IMMSignal, fourbitcompar_11_equal, ALUsrc);
  // AND_Gate and_12 has open pins: in0=fourbitcompar_12_equal, in1=ALUsrc, out=open
  buf and_13 (BSignal, fourbitcompar_13_equal);  // AND_Gate
  buf and_14 (CBZSignal, fourbitcompar_14_equal);  // AND_Gate
  buf and_15 (CBNZSignal, fourbitcompar_15_equal);  // AND_Gate

  assign SwapSignal = SWAP_bit;
endmodule

module ALU (
  input  [63:0] InputB,
  input  [63:0] InputA,
  input  ALUnum,
  input  [6:0] OPCODE,
  output [63:0] ALUout,
  output ZeroBit
);

  wire [63:0] adder_1_out, adder_2_out, adder_3_out, adder_4_out, divider_1_out, divider_1_rem,
       eightbyteand_1_output_bits, eightbyteor_1_output_bits, multiplexer_1_out, multiplexer_2_out,
       multiplier_1_out, negator_1_out, shifter_1_out, shifter_2_out, subtractor_1_out;

  Adder #(.width(64)) adder_1 (
    .a(InputA), .b({InputB[63:59], InputB[63:59], InputB[53:0]}), .out(adder_1_out));  // open: cin, cout
  Adder #(.width(64)) adder_2 (
    .a(InputA), .b({InputB[63:59], InputB[63:59], InputB[53:0]}), .out(adder_2_out));  // open: cin, cout
  Subtractor #(.width(64)) subtractor_1 (
    .a(InputA), .b({InputB[63:59], InputB[63:59], InputB[53:0]}), .out(subtractor_1_out));  // open: bin, bout
  Multiplier #(.mode("twosComplement"), .width(64)) multiplier_1 (
    .a(InputA), .b({InputB[63:59], InputB[63:59], InputB[53:0]}), .out(multiplier_1_out));  // open: cin, cout
  Divider #(.mode("twosComplement"), .width(64)) divider_1 (
    .a(InputA), .b({InputB[63:59], InputB[63:59], InputB[53:0]}), .out(divider_1_out), .rem(divider_1_rem));  // open: upper
  Shifter #(.width(64)) shifter_1 (.in(InputA), .\dist (InputB[5:0]), .out(shifter_1_out));
  Shifter #(.shift("ar"), .width(64)) shifter_2 (.in(InputA), .\dist (InputB[5:0]), .out(shifter_2_out));
  Negator #(.width(64)) negator_1 (.out(negator_1_out));  // open: in
  Adder #(.width(64)) adder_3 (
    .a({InputB[63:59], InputB[63:59], InputB[53:0]}), .b(InputA), .out(adder_3_out));  // open: cin, cout
  Multiplexer #(.enable("true"), .width(64)) multiplexer_1 (
    .in0({InputB[63:59], InputB[63:59], InputB[53:0]}), .in1(InputA), .out(multiplexer_1_out), .sel(ALUnum),
    .en(OPCODE[0]));
  Adder #(.width(64)) adder_4 (.a(negator_1_out), .b({64{1'b1}}), .out(adder_4_out));  // open: cin, cout
  EightByteAnd eightbyteand_1 (
    .InputA(InputA), .InputB({InputB[63:59], InputB[63:59], InputB[53:0]}),
    .Output_Bits(eightbyteand_1_output_bits));
  EightByteOr eightbyteor_1 (
    .InputA(InputA), .InputB({InputB[63:59], InputB[63:59], InputB[53:0]}),
    .Output_Bits(eightbyteor_1_output_bits));
  Multiplexer #(.width(64)) multiplexer_2 (.in0(InputA), .in1(adder_3_out), .out(multiplexer_2_out), .sel(OPCODE[1]));
  Multiplexer #(.select(5), .width(64)) multiplexer_3 (
    .in0(adder_1_out), .in1(adder_1_out), .in2(adder_1_out), .in3(adder_1_out), .in4(adder_1_out),
    .in5(adder_1_out), .in6(adder_1_out), .in7(adder_1_out), .in8(adder_1_out), .in9(adder_1_out),
    .in10(adder_1_out), .in11(adder_1_out), .in16(adder_2_out), .in17(subtractor_1_out),
    .in18(multiplier_1_out), .in19(divider_1_out), .in20(divider_1_rem), .in21(shifter_2_out),
    .in22(shifter_1_out), .in23(eightbyteand_1_output_bits), .in24(eightbyteor_1_output_bits),
    .in25(adder_4_out), .in26(multiplexer_2_out), .in27(multiplexer_1_out),
    .in28({InputB[63:59], InputB[63:59], InputB[53:0]}), .in29(InputA), .in30(InputA), .out(ALUout),
    .sel(OPCODE[6:2]));  // open: in12, in13, in14, in15, in31
  SixtyFourBitZeroChecker sixtyfourbitzerochecker_1 (.InputA(ALUout), .ZeroEqual(ZeroBit));

  assign InputB[58:54] = InputB[63:59];

  // Notes on the sheet:
  //   ADD
  //   MOD
  //   SUB
  //   MUL
  //   DIV
  //   LSL
  //   ASR
  //   NEG
  //   5 bits for instruction kind
endmodule

module WriteReg1 (
  input  WriteReg1_Exists,
  input  [31:0] EncodedInstruction,
  output [2:0] WriteReg_1
);

  Multiplexer #(.width(3)) multiplexer_1 (
    .in0(3'b111), .in1(EncodedInstruction[8:6]), .out(WriteReg_1), .sel(WriteReg1_Exists));
endmodule

module WriteReg2 (
  input  WriteReg2_Exists,
  input  [31:0] EncodedInstruction,
  output [2:0] WriteReg_2
);

  Multiplexer #(.width(3)) multiplexer_1 (
    .in0(3'b111), .in1(EncodedInstruction[5:3]), .out(WriteReg_2), .sel(WriteReg2_Exists));
endmodule

module WriteBack (
  input  [63:0] MemOutput,
  input  [63:0] ALUoutput,
  input  WriteALU,
  output [63:0] WBOutput
);

  Multiplexer #(.width(64)) multiplexer_1 (.in0(MemOutput), .in1(ALUoutput), .out(WBOutput), .sel(WriteALU));
endmodule

module SevenBitZeroCheck (
  input  [6:0] Bits,
  output Is_Zero
);

  wire or_1_out;

  or or_1 (or_1_out, Bits[0], Bits[1], Bits[2], Bits[3], Bits[4], Bits[5], Bits[6]);
  not not_1 (Is_Zero, or_1_out);
endmodule

module FourBitCompar (
  input  [3:0] Value,
  input  [3:0] Bits,
  output Equal
);

  wire not_1_out, not_2_out, not_3_out, not_4_out, xor_1_out, xor_2_out, xor_3_out, xor_4_out;

  xor xor_1 (xor_1_out, Value[0], Bits[0]);
  not not_1 (not_1_out, xor_1_out);
  xor xor_2 (xor_2_out, Value[1], Bits[1]);
  not not_2 (not_2_out, xor_2_out);
  xor xor_3 (xor_3_out, Value[2], Bits[2]);
  not not_3 (not_3_out, xor_3_out);
  xor xor_4 (xor_4_out, Value[3], Bits[3]);
  not not_4 (not_4_out, xor_4_out);
  and and_1 (Equal, not_1_out, not_2_out, not_3_out, not_4_out);
endmodule

module ALUControlSignalCreate (
  input  in_1,
  input  in_2
);
endmodule

module AppendZeroes (
  input  [15:0] Immediate,
  output [63:0] newImmediate
);


  assign newImmediate = {{48{1'b0}}, Immediate};
endmodule

module OneBitAnd (
  input  InputA,
  input  InputB,
  output Output1
);

  and and_1 (Output1, InputA, InputB);
endmodule

module EightBitAnd (
  input  [7:0] InputA,
  input  [7:0] InputB,
  output [7:0] OutputBits
);

  OneBitAnd onebitand_1 (.InputA(InputA[0]), .InputB(InputB[0]), .Output1(OutputBits[0]));
  OneBitAnd onebitand_2 (.InputA(InputA[1]), .InputB(InputB[1]), .Output1(OutputBits[1]));
  OneBitAnd onebitand_3 (.InputA(InputA[2]), .InputB(InputB[2]), .Output1(OutputBits[2]));
  OneBitAnd onebitand_4 (.InputA(InputA[3]), .InputB(InputB[3]), .Output1(OutputBits[3]));
  OneBitAnd onebitand_5 (.InputA(InputA[4]), .InputB(InputB[4]), .Output1(OutputBits[4]));
  OneBitAnd onebitand_6 (.InputA(InputA[5]), .InputB(InputB[5]), .Output1(OutputBits[5]));
  OneBitAnd onebitand_7 (.InputA(InputA[6]), .InputB(InputB[6]), .Output1(OutputBits[6]));
  OneBitAnd onebitand_8 (.InputA(InputA[7]), .InputB(InputB[7]), .Output1(OutputBits[7]));
endmodule

module EightByteAnd (
  input  [63:0] InputA,
  input  [63:0] InputB,
  output [63:0] Output_Bits
);

  EightBitAnd eightbitand_1 (.InputA(InputA[7:0]), .InputB(InputB[7:0]), .OutputBits(Output_Bits[7:0]));
  EightBitAnd eightbitand_2 (.InputA(InputA[15:8]), .InputB(InputB[15:8]), .OutputBits(Output_Bits[15:8]));
  EightBitAnd eightbitand_3 (.InputA(InputA[23:16]), .InputB(InputB[23:16]), .OutputBits(Output_Bits[23:16]));
  EightBitAnd eightbitand_4 (.InputA(InputA[31:24]), .InputB(InputB[31:24]), .OutputBits(Output_Bits[31:24]));
  EightBitAnd eightbitand_5 (.InputA(InputA[39:32]), .InputB(InputB[39:32]), .OutputBits(Output_Bits[39:32]));
  EightBitAnd eightbitand_6 (.InputA(InputA[47:40]), .InputB(InputB[47:40]), .OutputBits(Output_Bits[47:40]));
  EightBitAnd eightbitand_7 (.InputA(InputA[55:48]), .InputB(InputB[55:48]), .OutputBits(Output_Bits[55:48]));
  EightBitAnd eightbitand_8 (.InputA(InputA[63:56]), .InputB(InputB[63:56]), .OutputBits(Output_Bits[63:56]));
endmodule

module OneBitOr (
  input  InputA,
  input  InputB,
  output Output1
);

  or or_1 (Output1, InputA, InputB);
endmodule

module EightBitOr (
  input  [7:0] InputA,
  input  [7:0] InputB,
  output [7:0] OutputBits
);

  OneBitOr onebitor_1 (.InputA(InputA[0]), .InputB(InputB[0]), .Output1(OutputBits[0]));
  OneBitOr onebitor_2 (.InputA(InputA[1]), .InputB(InputB[1]), .Output1(OutputBits[1]));
  OneBitOr onebitor_3 (.InputA(InputA[2]), .InputB(InputB[2]), .Output1(OutputBits[2]));
  OneBitOr onebitor_4 (.InputA(InputA[3]), .InputB(InputB[3]), .Output1(OutputBits[3]));
  OneBitOr onebitor_5 (.InputA(InputA[4]), .InputB(InputB[4]), .Output1(OutputBits[4]));
  OneBitOr onebitor_6 (.InputA(InputA[5]), .InputB(InputB[5]), .Output1(OutputBits[5]));
  OneBitOr onebitor_7 (.InputA(InputA[6]), .InputB(InputB[6]), .Output1(OutputBits[6]));
  OneBitOr onebitor_8 (.InputA(InputA[7]), .InputB(InputB[7]), .Output1(OutputBits[7]));
endmodule

module EightByteOr (
  input  [63:0] InputA,
  input  [63:0] InputB,
  output [63:0] Output_Bits
);

  EightBitOr eightbitor_1 (.InputA(InputA[7:0]), .InputB(InputB[7:0]), .OutputBits(Output_Bits[7:0]));
  EightBitOr eightbitor_2 (.InputA(InputA[15:8]), .InputB(InputB[15:8]), .OutputBits(Output_Bits[15:8]));
  EightBitOr eightbitor_3 (.InputA(InputA[23:16]), .InputB(InputB[23:16]), .OutputBits(Output_Bits[23:16]));
  EightBitOr eightbitor_4 (.InputA(InputA[31:24]), .InputB(InputB[31:24]), .OutputBits(Output_Bits[31:24]));
  EightBitOr eightbitor_5 (.InputA(InputA[39:32]), .InputB(InputB[39:32]), .OutputBits(Output_Bits[39:32]));
  EightBitOr eightbitor_6 (.InputA(InputA[47:40]), .InputB(InputB[47:40]), .OutputBits(Output_Bits[47:40]));
  EightBitOr eightbitor_7 (.InputA(InputA[55:48]), .InputB(InputB[55:48]), .OutputBits(Output_Bits[55:48]));
  EightBitOr eightbitor_8 (.InputA(InputA[63:56]), .InputB(InputB[63:56]), .OutputBits(Output_Bits[63:56]));
endmodule

module SixtyFourBitZeroChecker (
  input  [63:0] InputA,
  output ZeroEqual
);

  wire or_1_out;

  or or_1 (or_1_out, InputA[0], InputA[1], InputA[2], InputA[3], InputA[4], InputA[5], InputA[6], InputA[7], InputA[8], InputA[9], InputA[10], InputA[11], InputA[12], InputA[13], InputA[14], InputA[15], InputA[16], InputA[17], InputA[18], InputA[19], InputA[20], InputA[21], InputA[22], InputA[23], InputA[24], InputA[25], InputA[26], InputA[27], InputA[28], InputA[29], InputA[30], InputA[31], InputA[32], InputA[33], InputA[34], InputA[35], InputA[36], InputA[37], InputA[38], InputA[39], InputA[40], InputA[41], InputA[42], InputA[43], InputA[44], InputA[45], InputA[46], InputA[47], InputA[48], InputA[49], InputA[50], InputA[51], InputA[52], InputA[53], InputA[54], InputA[55], InputA[56], InputA[57], InputA[58], InputA[59], InputA[60], InputA[61], InputA[62], InputA[63]);
  not not_1 (ZeroEqual, or_1_out);
endmodule

module SignedBitExtender (
  input  [7:0] EightBitInput,
  output [63:0] SignedOutput
);


  assign SignedOutput = {{57{EightBitInput[7]}}, EightBitInput[6:0]};
endmodule

module NormalBitExtender (
  input  [7:0] EightBitInput,
  output [63:0] NormalOutput
);


  assign NormalOutput = {{56{1'b0}}, EightBitInput};
endmodule

module ExtractSixteenBits (
  input  [63:0] InputA,
  output [15:0] OutputBits
);


  assign OutputBits = InputA[15:0];
endmodule

module ExtractEightBits (
  input  [63:0] InputA,
  output [7:0] Output16
);


  assign Output16 = InputA[7:0];
endmodule

module SignedBitExtender2 (
  input  [15:0] InputA,
  output [63:0] OutputA
);


  assign OutputA = {{49{InputA[15]}}, InputA[14:0]};
endmodule
